# Fritzing sketch serial-spy (saved by Fritzing 0.9.0b)

parts:
  Composant2 = Bluetooth Mate Silver
  Composant3 = Arduino Due (Rev2b)

nets:
  N1: Composant2.TX_5V, Composant3.D19/RX1
  GND: Composant2.GND, Composant3.GND

notes:
  Rx
  Tx
  GND
